# Fritzing sketch Tisley Park Original (saved by Fritzing 0.9.3b)
breadboards: 1

parts:
  Power_plug1 = Power plug
  Raspberry_Pi_Zero1 = Raspberry Pi Zero
  LM1 = RioRand LM2596
  S1 = Round Pushbutton
  LED1 = smd LED [color="Red (633nm)" package="0805 [SMD]"]
  Q1 = MOSFET-NCHANNEL [package=to220v]

nets:
  N1: Power_plug1.VCC, LED1.cathode
  N2: Power_plug1.GND, S1.leg1, Q1.S
  N3: Raspberry_Pi_Zero1.GPIO23, S1.leg0
  N4: Raspberry_Pi_Zero1.GPIO18, Q1.G
  N5: Raspberry_Pi_Zero1.GND, LM1.Pin_3
  N6: Raspberry_Pi_Zero1.5V, LM1.Pin_2
  N7: LED1.anode, Q1.D
