# Fritzing sketch Tisley Park Ring (saved by Fritzing 0.9.3b)
breadboards: 1

parts:
  Raspberry_Pi_Zero2 = Raspberry Pi Zero
  Power_plug2 = Power plug
  LM2 = RioRand LM2596
  S2 = Round Pushbutton
  Part1 = 16 NeoPixel Ring [part_number=1463]
  D1 = Rectifier Diode [part_number=1N4001 package="300 mil [THT]"]

nets:
  N1: Raspberry_Pi_Zero2.GPIO23, S2.leg0
  N2: Raspberry_Pi_Zero2.GPIO18, Part1.IN
  N3: Raspberry_Pi_Zero2.GND, LM2.Pin_3
  N4: Raspberry_Pi_Zero2.5V, LM2.Pin_2, D1.anode
  GND: Power_plug2.GND, S2.leg1, Part1.GND
  N5: Part1.VDD, D1.cathode

custom parts:
  16 NeoPixel Ring: 16 ultra bright smart LED NeoPixels are arranged in a circle with 1.75" (44.5mm) outer diameter. The rings are 'chainable' - connect the output pin of one to the input pin of another. Use only one microcontroller pin to control as many as you can chain together! Each LED is addressable as the driver chip is inside the LED. Each one has ~18mA constant current drive so the color will be very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
